# Fritzing sketch epinal_salon (saved by Fritzing 0.9.3b)

parts:
  LED1 = LED - 3mm [color="Yellow (595nm)" package="3 mm [THT]"]
  R1 = Resistor [tolerance=±5% resistance=4.7k package="2512 [SMD]"]
  DS1 = DS18B20 1-Wire Temperature Sensor [part_number=DS18B20]
  R2 = Resistor [tolerance=±5% resistance=1k package="2512 [SMD]"]
  Grove1 = Grove OLED 128x96
  WeMos_D1_Mini_Protoboard_Shield1 = WeMos D1 Mini Protoboard Shield
  Tx1 = mystery part, 3 pins [chip_label="433 Mhz"]

nets:
  N1: LED1.cathode, WeMos_D1_Mini_Protoboard_Shield1.X4-Y6
  N2: LED1.anode, WeMos_D1_Mini_Protoboard_Shield1.D8, WeMos_D1_Mini_Protoboard_Shield1.X2-Y7
  N3: R1.Pin_0, WeMos_D1_Mini_Protoboard_Shield1.X6-Y6
  N4: R1.Pin_1, WeMos_D1_Mini_Protoboard_Shield1.X6-Y10
  N5: DS1.GND, WeMos_D1_Mini_Protoboard_Shield1.X8-Y11
  N6: DS1.DQ, WeMos_D1_Mini_Protoboard_Shield1.D4, WeMos_D1_Mini_Protoboard_Shield1.X7-Y6
  N7: DS1.VDD, WeMos_D1_Mini_Protoboard_Shield1.X8-Y10
  N8: R2.Pin_0, WeMos_D1_Mini_Protoboard_Shield1.X4-Y7
  N9: R2.Pin_1, WeMos_D1_Mini_Protoboard_Shield1.X4-Y11
  N10: Grove1.GND, WeMos_D1_Mini_Protoboard_Shield1.X6-Y11
  N11: Grove1.VCC, WeMos_D1_Mini_Protoboard_Shield1.X5-Y10
  N12: Grove1.SDA, WeMos_D1_Mini_Protoboard_Shield1.D5, WeMos_D1_Mini_Protoboard_Shield1.X2-Y4
  N13: Grove1.SCL, WeMos_D1_Mini_Protoboard_Shield1.D6, WeMos_D1_Mini_Protoboard_Shield1.X2-Y5
  N14: WeMos_D1_Mini_Protoboard_Shield1.D3, WeMos_D1_Mini_Protoboard_Shield1.X7-Y5, Tx1.pin1
  N15: WeMos_D1_Mini_Protoboard_Shield1.X7-Y7, WeMos_D1_Mini_Protoboard_Shield1.X9-Y11
  N16: WeMos_D1_Mini_Protoboard_Shield1.X7-Y8, WeMos_D1_Mini_Protoboard_Shield1.X9-Y10
  N17: WeMos_D1_Mini_Protoboard_Shield1.X7-Y10, Tx1.pin2
  N18: WeMos_D1_Mini_Protoboard_Shield1.X7-Y11, Tx1.pin3
