# Fritzing sketch fil_pilote (saved by Fritzing 0.9.3b)
breadboards: 1

parts:
  Relay_5V = Keyes Relay [package=THT]
  WeMos_D1_Mini1 = WeMos D1 Mini
  Relay_5V1 = Keyes Relay [package=THT]
  D1 = Rectifier Diode [part_number=1N4007 package="300 mil [THT]"]
  D2 = Rectifier Diode [part_number=1N4007 package="300 mil [THT]"]
  LTR_1 = Monacor line transformer [part_number=LTR-110]
  J1 = screw terminal, 3 pins

nets:
  N1: Relay_5V.signal, WeMos_D1_Mini1.D5
  N2: Relay_5V.power, WeMos_D1_Mini1.5V, Relay_5V1.power, LTR_1.06
  N3: Relay_5V.ground, WeMos_D1_Mini1.G, Relay_5V1.ground, LTR_1.GND, J1.pin1
  N4: Relay_5V.NC, Relay_5V.C, Relay_5V.NO, Relay_5V1.C, D1.anode, LTR_1.05, J1.pin2
  N5: WeMos_D1_Mini1.D6, Relay_5V1.signal
  N6: Relay_5V1.NO, D2.cathode
  N7: D1.cathode, D2.anode, J1.pin3

custom parts:
  Keyes Relay: The Keyes 5V relay module is suitable for SCM development, home appliance control. It uses a 5V~12V TIL control signal which can control DC / AC signal.

// code stored in the sketch: bluetoothLight.ino
char blueToothVal;           //value sent over via bluetooth
char lastValue;              //stores last state of device (on/off)
 
void setup()
{
 Serial.begin(9600); 
 pinMode(13,OUTPUT);
 pinMode(12,INPUT);
}
 
 
void loop()
{
  if(Serial.available())
  {//if there is data being recieved
    blueToothVal=Serial.read(); //read it
  }
  if (blueToothVal=='n')
  {//if value from bluetooth serial is n
    digitalWrite(13,HIGH);            //switch on LED
    if (lastValue!='n')
      Serial.println(F("LED is on")); //print LED is on
    lastValue=blueToothVal;
  }
  else if (blueToothVal=='f')
  {//if value from bluetooth serial is n
    digitalWrite(13,LOW);             //turn off LED
    if (lastValue!='f')
      Serial.println(F("LED is off")); //print LED is on
    lastValue=blueToothVal;
  }
  delay(250);
}
