# Fritzing sketch poste_garage (saved by Fritzing 0.9.3b)
breadboards: 1

parts:
  WeMos_D1_Mini1 = WeMos D1 Mini
  IC3 = MCP3008 8-channel 10-bit ADC [part_number=MCP3008]
  ULN1 = Darlington Driver [package=dil18]
  U2 = QRD1114 [package=qrd1114]
  OMRON1 = OMRON PCB Power Relay – G5LE [part_number="G5LE-1\n" package=THT]
  U1 = QRD1114 [package=qrd1114]
  R1 = Resistor [tolerance=±5% resistance=220 package="2010 [SMD]"]
  R2 = Resistor [tolerance=±5% resistance=220 package="2010 [SMD]"]
  R3 = Resistor [tolerance=±5% resistance=4.7k package="1206 [SMD]"]
  R4 = Resistor [tolerance=±5% resistance=4.7k package="1206 [SMD]"]

nets:
  3V3: WeMos_D1_Mini1.3V3, IC3.Vref, IC3.Vdd, R1.Pin_1, R2.Pin_1, R3.Pin_1, R4.Pin_1
  N1: WeMos_D1_Mini1.D1, ULN1.1
  N2: WeMos_D1_Mini1.D5, IC3.CLK
  N3: WeMos_D1_Mini1.D6, IC3.Dout
  N4: WeMos_D1_Mini1.D7, IC3.Din
  N5: WeMos_D1_Mini1.D8, IC3.CS
  N6: WeMos_D1_Mini1.G, IC3.DGND, IC3.AGND, ULN1.9, U2.E, U2.K, U1.E, U1.K
  N7: IC3.CH0, U1.C, R3.Pin_0
  N8: IC3.CH1, U2.C, R4.Pin_0
  N9: ULN1.17, OMRON1.COIL1
  N10: ULN1.18, OMRON1.C
  N11: U2.A, R2.Pin_0
  N12: U1.A, R1.Pin_0
