# Fritzing sketch baie (saved by Fritzing 0.9.3b)
breadboards: 1

parts:
  WeMos_D1_Mini2 = WeMos D1 Mini
  Q1 = NPN-Transistor [package="TO92 [THT]"]
  J1 = Power Jack [package=power_jack_pth_lock]
  R1 = Resistor [tolerance=±5% resistance=3.3k package="1206 [SMD]"]
  R2 = Resistor [tolerance=±5% resistance=1k package="1206 [SMD]"]
  R3 = Resistor [tolerance=±5% resistance=4.7k package="1206 [SMD]"]
  D2 = Zener Diode [part_number=1N4732A breakdown_voltage=3.6V package="300 mil [THT]"]
  R4 = Resistor [tolerance=±5% resistance=1k package="1206 [SMD]"]
  C2 = Ceramic Capacitor [capacitance=100nF package="100 mil [THT, multilayer]"]
  U3 = Voltage Regulator - Variable [part_number=LM317T package="TO220 [THT]"]
  M1 = DC Motor
  DS1 = DS18B20 1-Wire Temperature Sensor [part_number=DS18B20]

nets:
  3V3: WeMos_D1_Mini2.3V3, R3.Pin_0, DS1.VDD
  N1: WeMos_D1_Mini2.5V, R1.Pin_1, U3.OUT
  N2: WeMos_D1_Mini2.D3, R4.Pin_1
  N3: WeMos_D1_Mini2.D4, R3.Pin_1, DS1.DQ
  GND: WeMos_D1_Mini2.G, Q1.E, J1.GND, R2.Pin_0, DS1.GND
  N4: Q1.B, R4.Pin_0
  N5: Q1.C, D2.anode, C2.0, M1.pin_2
  N6: J1.PWR, D2.cathode, C2.1, U3.IN, M1.pin_1
  N7: R1.Pin_0, R2.Pin_1, U3.ADJ
