# Fritzing sketch ballon (saved by Fritzing 0.9.1b)
breadboards: 1

parts:
  WeMos_D1_Mini1 = WeMos D1 Mini
  U1 = AD22100 - Voltage Output Temperature Sensor with Signal Conditioning [part_number=DS18B20]
  R1 = Resistor [tolerance=±5% resistance=4.7k package=THT]
  LED1 = LED - 5mm [color="Green (570nm)" package="5 mm [THT]"]
  R2 = Resistor [tolerance=±5% resistance=1k package=THT]
  IC1 = MICROCONTROLLER [package=dil28-3-simon]
  IC1_2 = MICROCONTROLLER [package=dil28-3-simon-kit]

nets:
  GND: WeMos_D1_Mini1.G, R2.Pin_0, IC1.GND, IC1_2.GND
  N1: U1.Data, R1.Pin_0
  N2: U1.Vcc, R1.Pin_1
  N3: LED1.cathode, R2.Pin_1
  N4: IC1.PC6(_RESET), IC1_2.PC6(_RESET)
  N5: IC1.PD0(RXD), IC1_2.PD0(RXD)
  N6: IC1.PD1(TXD), IC1_2.PD1(TXD)
  N7: IC1.PD2(INT0), IC1_2.PD2(INT0)
  N8: IC1.PD3(INT1), IC1_2.PD3(INT1)
  N9: IC1.PD4(XCK_T0), IC1_2.PD4(XCK_T0)
  VCC: IC1.VCC, IC1_2.VCC
  N10: IC1.PB6(XTAL1_TOSC1), IC1_2.PB6(XTAL1_TOSC1)
  N11: IC1.PB7(XTAL2_TOSC2), IC1_2.PB7(XTAL2_TOSC2)
  N12: IC1.PD5(T1), IC1_2.PD5(T1)
  N13: IC1.PD6(AIN0), IC1_2.PD6(AIN0)
  N14: IC1.PD7(AIN1), IC1_2.PD7(AIN1)
  N15: IC1.PB0(ICP), IC1_2.PB0(ICP)
  N16: IC1.PB1(OC1A), IC1_2.PB1(OC1A)
  N17: IC1.PB2(SS_OC1B), IC1_2.PB2(SS_OC1B)
  N18: IC1.PB3(MOSI_OC2), IC1_2.PB3(MOSI_OC2)
  N19: IC1.PB4(MISO), IC1_2.PB4(MISO)
  N20: IC1.PB5(SCK), IC1_2.PB5(SCK)
  N21: IC1.AVCC, IC1_2.AVCC
  N22: IC1.AREF, IC1_2.AREF
  N23: IC1.AGND, IC1_2.AGND
  N24: IC1.PC0(ADC0), IC1_2.PC0(ADC0)
  N25: IC1.PC1(ADC1), IC1_2.PC1(ADC1)
  N26: IC1.PC2(ADC2), IC1_2.PC2(ADC2)
  N27: IC1.PC3(ADC3), IC1_2.PC3(ADC3)
  N28: IC1.PC4(ADC4_SDA), IC1_2.PC4(ADC4_SDA)
  N29: IC1.PC5(ADC5_SCL), IC1_2.PC5(ADC5_SCL)

notes:
  Débitmètre

custom parts:
  WeMos D1 Mini: The D1 mini is a mini wifi board based on ESP-8266EX.
