# Fritzing sketch Gyrophare (saved by Fritzing 0.9.3b)
circuit board: 8.46667cm x 5.64444cm
breadboards: 1

parts:
  WeMos_D1_Mini_Protoboard_Shield1 = WeMos D1 Mini Protoboard Shield
  J1 = Piezo Speaker
  LED2 = LED - 5mm [color="White (4500K)" package="5 mm [THT]"]
  R1 = Resistor [tolerance=±5% resistance=220 package=THT]
  M1 = DC Motor
  C1 = Electrolytic Capacitor [capacitance=100nF package="100 mil [THT, electrolytic]"]
  R2 = Resistor [tolerance=±5% resistance=10k package=THT]
  D1 = Schottky Diode [part_number=1N5817 package="300 mil [THT]"]
  Q1 = Basic FET N-Channel [package="TO220 [THT]"]
  WeMos_D1_Mini1 = WeMos D1 Mini
  S1 = Pushbutton [package="[THT]"]

nets (from the breadboard view):
  N1: WeMos_D1_Mini_Protoboard_Shield1.X8-Y9, M1.pin_1, C1.-, D1.cathode, WeMos_D1_Mini1.5V
  N2: J1.pin1, R1.Pin_0, R2.Pin_0, Q1.source, WeMos_D1_Mini1.D4, S1.Pin_1, S1.Pin_2
  N3: J1.pin2, WeMos_D1_Mini1.D2
  N4: LED2.cathode, R1.Pin_1
  N5: LED2.anode, WeMos_D1_Mini1.D8
  N6: M1.pin_2, C1.+, D1.anode, Q1.drain
  N7: R2.Pin_1, Q1.gate, WeMos_D1_Mini1.D1
  N8: WeMos_D1_Mini1.D5, S1.Pin_3, S1.Pin_4
