# Fritzing sketch vmc_sdb (saved by Fritzing 0.9.3b)
breadboards: 1

parts:
  WeMos_D1_Mini1 = WeMos D1 Mini
  Relay_5V1 = Keyes Relay [package=THT]
  R1 = PHOTOCELL [package=photocell-kit]
  DHT1 = DHT11 Humitidy and Temperature Sensor
  R2 = Resistor [tolerance=±5% resistance=1k package=THT]
  R3 = Resistor [tolerance=±5% resistance=1k package=THT]
  R4 = Resistor [tolerance=±5% resistance=1k package=THT]

nets:
  N1: WeMos_D1_Mini1.3V3, R4.Pin_1
  5V: WeMos_D1_Mini1.5V, Relay_5V1.power, DHT1.VDD
  N2: WeMos_D1_Mini1.D0, R1.P$1, R2.Pin_1
  N3: WeMos_D1_Mini1.D1, Relay_5V1.signal
  N4: WeMos_D1_Mini1.D2, DHT1.DATA
  N5: WeMos_D1_Mini1.G, Relay_5V1.ground, DHT1.GND, R2.Pin_0
  N6: Relay_5V1.NC, Relay_5V1.C, Relay_5V1.NO
  N7: R1.P$2, R3.Pin_1
  N8: R3.Pin_0, R4.Pin_0

custom parts:
  Keyes Relay: The Keyes 5V relay module is suitable for SCM development, home appliance control. It uses a 5V~12V TIL control signal which can control DC / AC signal.
  DHT11 Humitidy and Temperature Sensor: DHT11 Humidity and Temperature Sensor

// code stored in the sketch: bluetoothLight.ino
char blueToothVal;           //value sent over via bluetooth
char lastValue;              //stores last state of device (on/off)
 
void setup()
{
 Serial.begin(9600); 
 pinMode(13,OUTPUT);
 pinMode(12,INPUT);
}
 
 
void loop()
{
  if(Serial.available())
  {//if there is data being recieved
    blueToothVal=Serial.read(); //read it
  }
  if (blueToothVal=='n')
  {//if value from bluetooth serial is n
    digitalWrite(13,HIGH);            //switch on LED
    if (lastValue!='n')
      Serial.println(F("LED is on")); //print LED is on
    lastValue=blueToothVal;
  }
  else if (blueToothVal=='f')
  {//if value from bluetooth serial is n
    digitalWrite(13,LOW);             //turn off LED
    if (lastValue!='f')
      Serial.println(F("LED is off")); //print LED is on
    lastValue=blueToothVal;
  }
  delay(250);
}
