# Fritzing sketch ballon_attiny (saved by Fritzing 0.9.3b)
breadboards: 1

parts:
  WeMos_D1_Mini1 = WeMos D1 Mini
  U1 = AD22100 - Voltage Output Temperature Sensor with Signal Conditioning [part_number=DS18B20]
  R1 = Resistor [tolerance=±5% resistance=4.7k package=THT]
  LED1 = LED - 5mm [color="Green (570nm)" package="5 mm [THT]"]
  R2 = Resistor [tolerance=±5% resistance=1k package=THT]
  U3 = ATTINY45 [package=dip]
  R3 = Resistor [tolerance=±5% resistance=2.2k package=THT]
  R4 = Resistor [tolerance=±5% resistance=1k package=THT]

nets:
  VCC: WeMos_D1_Mini1.5V, U1.Vcc, R1.Pin_1, U3.VCC
  N1: WeMos_D1_Mini1.G, U1.GND, R2.Pin_0, R3.Pin_0
  N2: U1.Data, R1.Pin_0
  N3: LED1.cathode, R2.Pin_1
  N4: U3.PB1(MISO), R4.Pin_1
  N5: R3.Pin_1, R4.Pin_0

notes:
  Débitmètre

custom parts:
  WeMos D1 Mini: The D1 mini is a mini wifi board based on ESP-8266EX.
